// Logisim project Projeto extreme (1).circ as structural Verilog
module \cronômetro  (
  output [3:0] out_1,
  output [3:0] out_2,
  output [3:0] out_3,
  output [3:0] out_4,
  output [3:0] out_5,
  output [3:0] out_6,
  output [3:0] out_7,
  output [3:0] out_8
);

  wire adder_1_out, and_1_out, and_2_out, and_3_out, and_4_out, and_5_out, and_6_out, button_1_out,
       clock_1_out, counter_2_carry, counter_3_carry, counter_4_carry, counter_5_q, counter_7_carry,
       counter_8_carry, counter_9_carry;

  and and_1 (and_1_out, counter_2_carry, counter_3_carry, counter_4_carry);
  Counter #(.width(4), .max('h9)) counter_1 (
    .count(and_1_out), .Q(out_5), .clk(and_3_out), .down(1'b1));  // open: load, D, carry, clr, preset
  and and_2 (and_2_out, counter_4_carry, counter_3_carry);
  Counter #(.width(4), .max('h9)) counter_2 (
    .count(and_2_out), .Q(out_6), .carry(counter_2_carry), .clk(and_3_out), .down(1'b1));  // open: load, D, clr, preset
  and and_3 (and_3_out, clock_1_out, counter_5_q);
  Clock clock_1 (.out(clock_1_out));
  Counter #(.width(4), .max('h5)) counter_3 (
    .count(counter_4_carry), .Q(out_7), .carry(counter_3_carry), .clk(and_3_out), .down(1'b1));  // open: load, D, clr, preset
  Counter #(.width(4), .max('h9)) counter_4 (
    .Q(out_8), .carry(counter_4_carry), .clk(and_3_out), .down(1'b1));  // open: load, D, count, clr, preset
  Adder #(.width(1)) adder_1 (.a(1'b1), .b(counter_5_q), .out(adder_1_out));  // open: cin, cout
  Counter #(.width(1), .max('h1)) counter_5 (
    .D(adder_1_out), .Q(counter_5_q), .clk(button_1_out));  // open: load, count, carry, clr, preset, down
  and and_4 (and_4_out, ~counter_5_q, clock_1_out);  // AND_Gate
  Button button_1 (.out(button_1_out));
  and and_5 (and_5_out, counter_7_carry, counter_8_carry, counter_9_carry);
  Counter #(.width(4), .max('h9)) counter_6 (
    .count(and_5_out), .Q(out_1), .clk(and_4_out), .down(1'b1));  // open: load, D, carry, clr, preset
  and and_6 (and_6_out, counter_9_carry, counter_8_carry);
  Counter #(.width(4), .max('h9)) counter_7 (
    .count(and_6_out), .Q(out_2), .carry(counter_7_carry), .clk(and_4_out), .down(1'b1));  // open: load, D, clr, preset
  Counter #(.width(4), .max('h5)) counter_8 (
    .count(counter_9_carry), .Q(out_3), .carry(counter_8_carry), .clk(and_4_out), .down(1'b1));  // open: load, D, clr, preset
  Counter #(.width(4), .max('h9)) counter_9 (
    .Q(out_4), .carry(counter_9_carry), .clk(and_4_out), .down(1'b1));  // open: load, D, count, clr, preset
endmodule

module cronometro_2 (
);

  wire clock_1_out, counter_2_carry;
  wire [3:0] counter_1_q, counter_2_q;

  Counter #(.width(4), .max('h5)) counter_1 (
    .count(counter_2_carry), .Q(counter_1_q), .clk(clock_1_out));  // open: load, D, carry, clr, preset, down
  Clock clock_1 (.out(clock_1_out));
  Hex_Digit_Display hex_digit_display_1 (.value(counter_1_q));  // open: dp
  Counter #(.width(4), .max('h9)) counter_2 (
    .Q(counter_2_q), .carry(counter_2_carry), .clk(clock_1_out));  // open: load, D, count, clr, preset, down
  Hex_Digit_Display hex_digit_display_2 (.value(counter_2_q));  // open: dp
endmodule

module GTN_X (
  input  CONFIRMAR,
  input  NOVO,
  input  [3:0] X,
  input  [3:0] Y,
  output X_CERTO,
  output Y_CERTO,
  output SOMA_CERTA,
  output [7:0] vermelho,
  output [7:0] azul
);

  wire comparator_1_eq, comparator_2_eq, comparator_3_eq;
  wire [4:0] \diferença_1_out_3 , somador_1_out_3, somador_2_out_3;
  wire [7:0] bit_extender_1_out, cores_1_azul, cores_1_vermelho, random_1_out;

  Random random_1 (.clk(NOVO), .out(random_1_out));  // open: next, clr
  assign bit_extender_1_out = {{7{1'b0}}, CONFIRMAR};  // Bit_Extender bit_extender_1
  somador somador_1 (.in_1(random_1_out[7:4]), .in_2(random_1_out[3:0]), .out_3(somador_1_out_3));
  somador somador_2 (.in_1(Y), .in_2(X), .out_3(somador_2_out_3));
  and and_1 (X_CERTO, CONFIRMAR, comparator_1_eq);
  Comparator #(.width(4)) comparator_1 (.a(random_1_out[3:0]), .b(X), .eq(comparator_1_eq));  // open: gt, lt
  and and_2 (Y_CERTO, CONFIRMAR, comparator_2_eq);
  Comparator #(.width(4)) comparator_2 (.a(random_1_out[7:4]), .b(Y), .eq(comparator_2_eq));  // open: gt, lt
  and and_3 (SOMA_CERTA, CONFIRMAR, comparator_3_eq);
  Comparator #(.width(5)) comparator_3 (
    .a(somador_1_out_3), .b(somador_2_out_3), .eq(comparator_3_eq));  // open: gt, lt
  \diferença  \diferença_1  (.X(somador_1_out_3), .Y(somador_2_out_3), .out_3(\diferença_1_out_3 ));
  assign vermelho = bit_extender_1_out & cores_1_vermelho;  // AND_Gate and_4, 8 bits wide
  cores cores_1 (.vermelho(cores_1_vermelho), .azul(cores_1_azul), .in_1(\diferença_1_out_3 ));
  assign azul = cores_1_azul & bit_extender_1_out;  // AND_Gate and_5, 8 bits wide

  // Notes on the sheet:
  //   somador
  //   comparador de 4b
  //   comp. de 4b
  //   comp. de 5b
  //   diferença
  //   cores
endmodule

module somador (
  input  [3:0] in_1,
  input  [3:0] in_2,
  output [4:0] out_3
);

  Adder #(.width(4)) adder_1 (.a(in_1), .b(in_2), .out(out_3[3:0]), .cout(out_3[4]));  // open: cin
endmodule

module \diferença  (
  input  [4:0] X,
  input  [4:0] Y,
  output [4:0] out_3
);

  wire comparator_1_gt;

  Comparator #(.width(5)) comparator_1 (.a(X), .b(Y), .gt(comparator_1_gt));  // open: eq, lt
  Adder #(.width(5)) adder_1 (.a(X), .b(Y), .out(out_3), .cout(comparator_1_gt));  // open: cin
endmodule

module cores (
  input  [4:0] in_1,
  output [7:0] vermelho,
  output [7:0] azul
);

  assign vermelho = ~{in_1, 3'b111};  // NOT_Gate not_1, 8 bits wide

  assign azul = {in_1, 3'b111};
endmodule
