// Logisim project Projeto extreme.circ as structural Verilog
module \cronômetro  (
);

  wire and_1_out, and_2_out, button_1_out, clock_1_out, register_1_q, subtractor_2_out;
  wire [3:0] counter_1_q, counter_2_q, subtractor_1_out, subtractor_3_out;

  Subtractor #(.width(4)) subtractor_1 (.a(counter_1_q), .b(4'b0001), .out(subtractor_1_out));  // open: bin, bout
  Hex_Digit_Display hex_digit_display_1 (.value(counter_1_q));  // open: dp
  Counter #(.width(4), .max('h9)) counter_1 (
    .D(subtractor_1_out), .Q(counter_1_q), .clk(and_1_out));  // open: load, count, carry, clr, preset, down
  and and_1 (and_1_out, clock_1_out, register_1_q);
  Clock clock_1 (.out(clock_1_out));
  Subtractor #(.width(1)) subtractor_2 (.a(1'b1), .b(register_1_q), .out(subtractor_2_out));  // open: bin, bout
  Register #(.width(1), .Select("low")) register_1 (
    .D(subtractor_2_out), .Q(register_1_q), .clk(button_1_out));  // open: en, clr
  Subtractor #(.width(4)) subtractor_3 (.a(counter_2_q), .b(4'b0001), .out(subtractor_3_out));  // open: bin, bout
  Button button_1 (.out(button_1_out));
  Counter #(.width(4), .max('h9)) counter_2 (
    .D(subtractor_3_out), .Q(counter_2_q), .clk(and_2_out));  // open: load, count, carry, clr, preset, down
  and and_2 (and_2_out, ~register_1_q, clock_1_out);  // AND_Gate
  Hex_Digit_Display hex_digit_display_2 (.value(counter_2_q));  // open: dp
endmodule

module cronometro_2 (
);

  wire clock_1_out, counter_1_carry;
  wire [3:0] counter_2_q, counter_3_q;

  Counter #(.width(4), .max('h5)) counter_1 (
    .carry(counter_1_carry), .clk(clock_1_out));  // open: load, D, count, Q, clr, preset, down
  Clock clock_1 (.out(clock_1_out));
  Hex_Digit_Display hex_digit_display_1 (.value(counter_2_q));  // open: dp
  Counter #(.width(4), .max('h5)) counter_2 (
    .Q(counter_2_q), .clk(clock_1_out), .down(counter_1_carry));  // open: load, D, count, carry, clr, preset
  Counter #(.width(4), .max('h9)) counter_3 (
    .Q(counter_3_q), .clk(clock_1_out));  // open: load, D, count, carry, clr, preset, down
  Hex_Digit_Display hex_digit_display_2 (.value(counter_3_q));  // open: dp
endmodule
